// Logisim project boolean_algebra.circ as structural Verilog: 1 circuit, main circuit main
module main (
  input  A_0,
  input  A_4,
  input  A_1,
  input  A_5,
  input  A_2,
  input  A_6,
  input  A_7,
  input  A_3,
  input  c_A_0,
  input  a_A_0,
  input  d_A_0,
  input  c_B_0,
  input  a_B_0,
  input  d_B_0,
  input  a_C_0,
  input  d_C_0,
  input  A,
  input  B,
  output r_A_0,
  output r_0,
  output r_1,
  output r_A_5,
  output r_A_2,
  output r_A_6,
  output r_0_0,
  output r_1_1,
  output A___B,
  output A____B___C,
  output out_29,
  output B___A,
  output out_31,
  output A___B_2,
  output out_33,
  output B___A_2,
  output A___B____C,
  output out_36,
  output A____B___C_2,
  output A____B___C_3,
  output out_39,
  output out_40,
  output out_41
);

  wire and_1_out, and_8_out, and_9_out, and_12_out, and_13_out, and_14_out, not_1_out, not_2_out, not_4_out,
       not_5_out, or_8_out, or_9_out, or_12_out, or_13_out, or_14_out;

  not not_1 (not_1_out, A);
  not not_2 (not_2_out, B);
  nand nand_1 (out_39, A, B);
  and and_1 (and_1_out, A, B);
  not not_3 (out_40, and_1_out);
  or or_1 (out_41, not_1_out, not_2_out);
  or or_2 (r_A_0, 1'b0, A_0);
  or or_3 (r_1, 1'b1, A_1);
  or or_4 (r_A_2, A_2, A_2);
  not not_4 (not_4_out, A_3);
  or or_5 (A___B, c_A_0, c_B_0);
  or or_6 (B___A, c_B_0, c_A_0);
  and and_2 (A___B_2, c_A_0, c_B_0);
  and and_3 (B___A_2, c_B_0, c_A_0);
  or or_7 (r_1_1, not_4_out, A_3);
  and and_4 (r_0, 1'b0, A_4);
  and and_5 (r_A_5, 1'b1, A_5);
  and and_6 (r_A_6, A_6, A_6);
  not not_5 (not_5_out, A_7);
  and and_7 (r_0_0, not_5_out, A_7);
  or or_8 (or_8_out, a_A_0, a_B_0);
  or or_9 (or_9_out, a_B_0, a_C_0);
  and and_8 (and_8_out, a_A_0, a_B_0);
  and and_9 (and_9_out, a_B_0, a_C_0);
  or or_10 (out_29, or_8_out, a_C_0);
  or or_11 (out_31, a_A_0, or_9_out);
  and and_10 (A___B____C, and_8_out, a_C_0);
  and and_11 (A____B___C_2, a_A_0, and_9_out);
  and and_12 (and_12_out, d_B_0, d_C_0);
  or or_12 (or_12_out, d_A_0, d_B_0);
  or or_13 (or_13_out, d_A_0, d_C_0);
  and and_13 (and_13_out, d_A_0, d_B_0);
  and and_14 (and_14_out, d_A_0, d_C_0);
  or or_14 (or_14_out, d_B_0, d_C_0);
  or or_15 (A____B___C, d_A_0, and_12_out);
  and and_15 (out_33, or_12_out, or_13_out);
  or or_16 (out_36, and_13_out, and_14_out);
  and and_16 (A____B___C_3, d_A_0, or_14_out);

  // Notes on the sheet:
  //   Commutative
  //   A + B = B + A 
  //   A * B = B * A 
  //   NAND gate is equal to an OR gate with inverted inputs
  //    The four possible logical OR operations
  //   Boolean Algebra
  //   Associative
  //   (A + B) + C = A + (B + C)  
  //   (A * B) * C = A * (B * C)
  //   The four possible logical AND operations:
  //   (A + B) + C
  //   A + (B + C)
  //   Distributive
  //   A + (B * C) = (A + B) * (A + C)  
  //   (A * B) + (A * C) = A * (B + C)
  //   (A + B) * (A + C)
  //   (A * B) + (A * C)
endmodule
