// Logisim project circuit2.circ as structural Verilog: 1 circuit, main circuit main
module main (
  input  A,
  input  B,
  input  C,
  output Output_D,
  output Output_E
);

  wire and_1_out, and_2_out, and_3_out, and_4_out, and_5_out, and_6_out, and_7_out, and_8_out, and_9_out,
       not_1_out, not_2_out, not_3_out, not_4_out, or_1_out, or_2_out;

  not not_1 (not_1_out, A);
  not not_2 (not_2_out, C);
  not not_3 (not_3_out, A);
  and and_1 (and_1_out, not_1_out, B);
  and and_2 (and_2_out, not_3_out, B);
  and and_3 (and_3_out, A, B);
  and and_4 (and_4_out, A, B);
  and and_5 (and_5_out, A, not_4_out);
  not not_4 (not_4_out, B);
  and and_6 (and_6_out, and_1_out, not_2_out);
  and and_7 (and_7_out, and_2_out, C);
  and and_8 (and_8_out, and_3_out, not_2_out);
  and and_9 (and_9_out, and_4_out, C);
  and and_10 (Output_E, and_5_out, C);
  or or_1 (or_1_out, and_6_out, and_7_out);
  or or_2 (or_2_out, and_8_out, and_9_out);
  or or_3 (Output_D, or_1_out, or_2_out);

  // Notes on the sheet:
  //   E = A * `B * C 
  //   D = (`A * B * `C) + (`A * B * C) + (A * B * `C) + (A * B * C)
endmodule
