// Logisim project ALU.circ as structural Verilog: 1 circuit, main circuit main
module main (
  input  [1:0] OPERATION,
  input  A,
  input  B,
  input  CarryIn,
  output Result,
  output CarryOut
);

  wire and_1_out, and_2_out, and_3_out, and_4_out, and_5_out, and_6_out, and_7_out, not_1_out, not_2_out,
       not_3_out, not_4_out, or_1_out, or_2_out, or_3_out;

  not not_1 (not_1_out, A);
  not not_2 (not_2_out, B);
  and and_1 (and_1_out, not_1_out, B);
  and and_2 (and_2_out, A, not_2_out);
  and and_3 (and_3_out, A, B);
  and and_4 (and_4_out, A, B);
  or or_1 (or_1_out, A, B);
  or or_2 (or_2_out, and_1_out, and_2_out);
  not not_3 (not_3_out, or_2_out);
  not not_4 (not_4_out, CarryIn);
  and and_5 (and_5_out, not_3_out, CarryIn);
  and and_6 (and_6_out, or_2_out, not_4_out);
  and and_7 (and_7_out, or_2_out, CarryIn);
  or or_3 (or_3_out, and_5_out, and_6_out);
  or or_4 (CarryOut, and_3_out, and_7_out);
  Multiplexer #(.enable("false"), .select(2)) multiplexer_1 (
    .in0(and_4_out), .in1(and_4_out), .in2(or_1_out), .in3(or_3_out), .out(Result), .sel(OPERATION));

  // Notes on the sheet:
  //   ALU
endmodule
