// Logisim project ALU_ALL.circ as structural Verilog
module half_adder (
  input  A,
  input  B,
  output Carry,
  output Sum
);

  wire and_1_out, and_2_out, not_1_out, not_2_out;

  not not_1 (not_1_out, A);
  not not_2 (not_2_out, B);
  and and_1 (and_1_out, not_1_out, B);
  and and_2 (and_2_out, A, not_2_out);
  and and_3 (Carry, A, B);
  or or_1 (Sum, and_1_out, and_2_out);
endmodule

module full_adder (
  input  A,
  input  B,
  input  CarryIn,
  output CarryOut,
  output Sum
);

  wire half_adder_1_carry, half_adder_1_sum, half_adder_2_carry;

  half_adder half_adder_1 (.A(A), .B(B), .Carry(half_adder_1_carry), .Sum(half_adder_1_sum));
  half_adder half_adder_2 (.A(half_adder_1_sum), .B(CarryIn), .Carry(half_adder_2_carry), .Sum(Sum));
  or or_1 (CarryOut, half_adder_1_carry, half_adder_2_carry);
endmodule

module ALU (
  input  CarryIn,
  input  B,
  input  A,
  input  [1:0] Operation,
  output Result,
  output CarryOut
);

  wire and_1_out, full_adder_1_sum, or_1_out;

  and and_1 (and_1_out, A, B);
  or or_1 (or_1_out, A, B);
  full_adder full_adder_1 (.A(A), .B(B), .CarryIn(CarryIn), .CarryOut(CarryOut), .Sum(full_adder_1_sum));
  Multiplexer #(.enable("false"), .select(2)) multiplexer_1 (
    .in0(and_1_out), .in1(or_1_out), .in2(full_adder_1_sum), .out(Result), .sel(Operation));  // open: in3

  // Notes on the sheet:
  //   Operation 00 is Logical AND
  //   Operation 01 is Logical OR
  //   Operation 10 is Addition
endmodule

module Adder_4bit (
  input  CarryIn,
  input  B3,
  input  B2,
  input  B1,
  input  B0,
  input  A3,
  input  A2,
  input  A1,
  input  A0,
  output Cout,
  output Sum3,
  output Sum2,
  output Sum1,
  output Sum0
);

  wire full_adder_1_carryout, full_adder_2_carryout, full_adder_3_carryout;

  full_adder full_adder_1 (.A(A0), .B(B0), .CarryIn(CarryIn), .CarryOut(full_adder_1_carryout), .Sum(Sum0));
  full_adder full_adder_2 (
    .A(A1), .B(B1), .CarryIn(full_adder_1_carryout), .CarryOut(full_adder_2_carryout), .Sum(Sum1));
  full_adder full_adder_3 (
    .A(A2), .B(B2), .CarryIn(full_adder_2_carryout), .CarryOut(full_adder_3_carryout), .Sum(Sum2));
  full_adder full_adder_4 (.A(A3), .B(B3), .CarryIn(full_adder_3_carryout), .CarryOut(Cout), .Sum(Sum3));
endmodule

module Adder_8bits (
  input  in_1
);

  wire adder_4bit_1_cout, undriven, undriven_2;

  Adder_4bit adder_4bit_1 (
    .CarryIn(in_1), .B3(undriven), .B2(undriven_2), .Cout(adder_4bit_1_cout));  // open: B1, B0, A3, A2, A1, A0, Sum3, Sum2, Sum1, Sum0
  Adder_4bit adder_4bit_2 (.CarryIn(adder_4bit_1_cout));  // open: B3, B2, B1, B0, A3, A2, A1, A0, Cout, Sum3, Sum2, Sum1, Sum0
endmodule

module ALU4 (
  input  CarryIn,
  input  B3,
  input  B2,
  input  B1,
  input  B0,
  input  A3,
  input  A2,
  input  A1,
  input  A0,
  input  [1:0] OpCode,
  output CarryOut,
  output R3,
  output R2,
  output R1,
  output R0
);

  wire alu_1_carryout, alu_2_carryout, alu_3_carryout;

  ALU alu_1 (.CarryIn(CarryIn), .B(B0), .A(A0), .Operation(OpCode), .Result(R0), .CarryOut(alu_1_carryout));
  ALU alu_2 (.CarryIn(alu_1_carryout), .B(B1), .A(A1), .Operation(OpCode), .Result(R1), .CarryOut(alu_2_carryout));
  ALU alu_3 (.CarryIn(alu_2_carryout), .B(B2), .A(A2), .Operation(OpCode), .Result(R2), .CarryOut(alu_3_carryout));
  ALU alu_4 (.CarryIn(alu_3_carryout), .B(B3), .A(A3), .Operation(OpCode), .Result(R3), .CarryOut(CarryOut));

  // Notes on the sheet:
  //   Operation 00 is Logical AND
  //   Operation 01 is Logical OR
  //   Operation 10 is Addition
endmodule

module InfiniteHardware (
  input  CarryIn,
  input  B3,
  input  B2,
  input  B1,
  input  B0,
  input  A3,
  input  A2,
  input  A1,
  input  A0,
  output Cout,
  output Sum3,
  output Sum2,
  output Sum1,
  output Sum0
);

  wire and_4_out, full_adder_3_carryout, undriven, undriven_2;

  // AND_Gate and_1 has open pins: in1=undriven, out=open
  // AND_Gate and_2 is placed but not wired
  // AND_Gate and_3 is placed but not wired
  and and_4 (and_4_out, A0, B0);
  full_adder full_adder_1 (.A(A0), .B(B0), .CarryIn(CarryIn), .Sum(Sum0));  // open: CarryOut
  full_adder full_adder_2 (.A(A1), .B(B1), .CarryIn(and_4_out), .Sum(Sum1));  // open: CarryOut
  full_adder full_adder_3 (.A(A2), .B(B2), .CarryIn(undriven_2), .CarryOut(full_adder_3_carryout), .Sum(Sum2));
  full_adder full_adder_4 (.A(A3), .B(B3), .CarryIn(full_adder_3_carryout), .CarryOut(Cout), .Sum(Sum3));
endmodule

module Adder_4bits_Rev (
  input  CarryIn,
  input  B3,
  input  B2,
  input  B1,
  input  B0,
  input  A3,
  input  A2,
  input  A1,
  input  A0,
  output Cout,
  output Sum3,
  output Sum2,
  output Sum1,
  output Sum0
);

  wire and_1_out, and_2_out, and_3_out, and_4_out, and_5_out, and_6_out, C1, C2, C3;

  and and_1 (and_1_out, C1, B1);
  and and_2 (and_2_out, C1, A1);
  and and_3 (and_3_out, A1, B1);
  or or_1 (C2, and_1_out, and_2_out, and_3_out);
  and u_C1 (C1, A0, B0);
  and and_4 (and_4_out, C2, B2);
  and and_5 (and_5_out, C2, A2);
  and and_6 (and_6_out, A2, B2);
  or or_2 (C3, and_4_out, and_5_out, and_6_out);
  full_adder full_adder_1 (.A(A0), .B(B0), .CarryIn(CarryIn), .Sum(Sum0));  // open: CarryOut
  full_adder full_adder_2 (.A(A1), .B(B1), .CarryIn(C1), .Sum(Sum1));  // open: CarryOut
  full_adder full_adder_3 (.A(A2), .B(B2), .CarryIn(C2), .Sum(Sum2));  // open: CarryOut
  full_adder full_adder_4 (.A(A3), .B(B3), .CarryIn(C3), .CarryOut(Cout), .Sum(Sum3));
endmodule
