// Logisim project Intro.circ as structural Verilog: 1 circuit, main circuit main
module main (
  input  Inputs,
  input  in_2,
  input  in_3,
  input  in_4,
  input  in_5,
  input  in_6,
  input  in_7,
  input  in_8,
  input  in_9,
  input  in_10,
  input  in_11,
  input  in_12,
  input  in_13,
  output out_14,
  output out_15,
  output out_16,
  output out_17,
  output out_18,
  output out_19,
  output out_20
);

  wire and_2_out;

  and and_1 (out_14, Inputs, in_2);
  or or_1 (out_15, in_3, in_4);
  not not_1 (out_16, in_5);
  xor xor_1 (out_17, in_6, in_7);
  nand nand_1 (out_18, in_8, in_10);
  nor nor_1 (out_20, in_12, in_13);
  and and_2 (and_2_out, in_9, in_11);
  not not_2 (out_19, and_2_out);

  // Notes on the sheet:
  //   AND Gate
  //   OR Gate
  //   NOT Gate
  //   XOR Gate
  //   NAND Gate
  //   NOR Gate
  //   One Output
  //   THIS IS THE SAME AS A NAND
endmodule
