// Logisim project boolean_expression1.circ as structural Verilog: 1 circuit, main circuit main
module main (
  input  A,
  input  B,
  input  C,
  output Q,
  output Simplify_Q
);

  wire and_1_out, and_2_out, and_3_out, and_4_out, and_5_out, and_6_out, and_7_out, and_8_out, not_1_out,
       not_2_out, or_1_out, or_2_out;

  not not_1 (not_1_out, A);
  not not_2 (not_2_out, B);
  not not_3 (Simplify_Q, C);
  and and_1 (and_1_out, not_1_out, not_2_out);
  and and_2 (and_2_out, not_1_out, B);
  and and_3 (and_3_out, A, not_2_out);
  and and_4 (and_4_out, A, B);
  and and_5 (and_5_out, and_1_out, Simplify_Q);
  and and_6 (and_6_out, and_2_out, Simplify_Q);
  and and_7 (and_7_out, and_3_out, Simplify_Q);
  and and_8 (and_8_out, and_4_out, Simplify_Q);
  or or_1 (or_1_out, and_5_out, and_6_out);
  or or_2 (or_2_out, and_7_out, and_8_out);
  or or_3 (Q, or_1_out, or_2_out);

  // Notes on the sheet:
  //   Q = f(a,b,c) = (`A * `B * `C) + (`A * B * `C) + (A * `B * `C) + (A * B * `C)
  //   Q = f(a,b,c) = `C
endmodule
