// Logisim project boolean_expression2.circ as structural Verilog: 1 circuit, main circuit main
module main (
  input  A,
  input  B,
  input  in_3,
  input  in_4,
  output Q,
  output out_6,
  output out_7,
  output out_8
);

  wire and_1_out, and_2_out, and_4_out, not_1_out, not_2_out;

  not not_1 (not_1_out, A);
  and and_1 (and_1_out, not_1_out, B);
  and and_2 (and_2_out, A, B);
  and and_3 (out_6, A, B);
  and and_4 (and_4_out, and_1_out, A);
  or or_1 (Q, and_4_out, and_2_out);
  not not_2 (not_2_out, in_3);
  and and_5 (out_7, not_2_out, in_3);
  and and_6 (out_8, in_4, 1'b0);

  // Notes on the sheet:
  //   Q = f(a,b) = (`A * B * A) + (A * B)
  //   Q = f(a,b) = (A * B)
endmodule
