// Logisim project circuit1.circ as structural Verilog: 1 circuit, main circuit main
module main (
  input  A,
  input  B,
  output Output_C
);

  wire and_1_out, and_2_out, not_1_out;

  not not_1 (not_1_out, A);
  and and_1 (and_1_out, not_1_out, B);
  and and_2 (and_2_out, A, B);
  or or_1 (Output_C, and_1_out, and_2_out);

  // Notes on the sheet:
  //   C = (`A * B) + (A * B)
endmodule
