// Logisim project full_adder.circ as structural Verilog
module full_adder (
  input  A,
  input  B,
  input  CarryIn,
  output Carry,
  output Sum
);

  wire and_1_out, and_2_out, and_3_out, and_4_out, and_5_out, not_1_out, not_2_out;

  not not_1 (not_1_out, A);
  not not_2 (not_2_out, B);
  and and_1 (and_1_out, not_1_out, B);
  and and_2 (and_2_out, A, not_2_out);
  and and_3 (and_3_out, A, B);
  and and_4 (and_4_out, A, CarryIn);
  and and_5 (and_5_out, B, CarryIn);
  or or_1 (Sum, and_1_out, and_2_out);
  or or_2 (Carry, and_3_out, and_4_out, and_5_out);
endmodule
