// Logisim project half_adder.circ as structural Verilog: 2 circuits, main circuit half_adder
module half_adder (
  input  A,
  input  B,
  output Carry,
  output Sum
);

  wire and_1_out, and_2_out, not_1_out, not_2_out;

  not not_1 (not_1_out, A);
  not not_2 (not_2_out, B);
  and and_1 (and_1_out, not_1_out, B);
  and and_2 (and_2_out, A, not_2_out);
  and and_3 (Carry, A, B);
  or or_1 (Sum, and_1_out, and_2_out);

  // Notes on the sheet:
  //   Half Adder
  //   SUM = f(a,b) = (`A * B) + (A * `B)
endmodule

module HalfAdder (
  input  in_1,
  input  in_2,
  output out_3,
  output out_4
);

  half_adder half_adder_1 (.A(in_1), .B(in_2), .Carry(out_3), .Sum(out_4));
endmodule
