// Logisim project mux1.circ as structural Verilog: 1 circuit, main circuit main
module main (
  input  A,
  input  B,
  input  SELECTOR,
  output OUT_0,
  output OUT_00
);

  wire and_1_out, and_2_out, not_1_out;

  not not_1 (not_1_out, SELECTOR);
  and and_1 (and_1_out, A, not_1_out);
  and and_2 (and_2_out, SELECTOR, B);
  or or_1 (OUT_0, and_1_out, and_2_out);
  Multiplexer #(.enable("false")) multiplexer_1 (.in0(A), .in1(B), .out(OUT_00), .sel(SELECTOR));

  // Other names for the same wires on the sheet: INPUT_A = A; INPUT_B = B; SELECTOR_T = SELECTOR

  // Notes on the sheet:
  //   SELECT 0 ==> OUTPUT IS INPUT A
  //   SELECT 1 ==> OUTPUT IS INPUT B
endmodule
